# Fritzing sketch dioramaEffects (saved by Fritzing 0.9.3b)
breadboards: 1

parts:
  Arduino = Arduino Pro Mini v13
  1N4001_DIODE_PUMP = Diode [package=diode-1n4148]  # not connected
  R1_220_RED = Resistor [tolerance=±5% resistance=220 package="0603 [SMD]"]
  R2_220_GREEN = Resistor [tolerance=±5% resistance=220 package="0603 [SMD]"]
  R3_220_BLUE = Resistor [tolerance=±5% resistance=220 package="0603 [SMD]"]
  U1 = Voltage Regulator [package=to220-adj]  # not connected
  R_1K_ACTIVATOR = Resistor [tolerance=±5% resistance=1k package="1206 [SMD]"]  # not connected
  LIGHT_EFFECT_SWITCH = Toggle Switch [package=THT]  # not connected
  TIMER_SWITCH = Toggle Switch [package=THT]  # not connected
  ACTIVATOR_BUTTON = Momentary Switch [package=ksa_sealed_tac_switch]  # not connected
  PIR_SENSOR = PIR sensor  # not connected
  PN2222_TRANSISTOR_PUMP = TRANSISTOR_PNP [package=to-92]  # not connected
  R5_330_PUMP = Resistor [tolerance=±5% resistance=330 package="0603 [SMD]"]  # not connected
  LED1 = RGB LED - (4 legs) [package="5 mm [THT]"]

nets:
  N1: Arduino.D8, R1_220_RED.Pin_1
  N2: Arduino.D7, R2_220_GREEN.Pin_1
  N3: Arduino.D6_PWM, R3_220_BLUE.Pin_1
  N4: R1_220_RED.Pin_0, LED1.red_cathode
  N5: R2_220_GREEN.Pin_0, LED1.green_cathode
  N6: R3_220_BLUE.Pin_0, LED1.blue_cathode
